# Fritzing sketch circuit (saved by Fritzing 1.0.4)
breadboards: 1

parts:
  R1 = Resistor [tolerance=±5% power=0.25W resistance=10000 package=THT]
  R2 = Resistor [tolerance=±5% power=0.25W resistance=1000000 package=THT]
  R3 = Resistor [tolerance=±5% power=0.25W resistance=10000 package=THT]
  Part1 = Arduino Nano (Rev3.0)
  J1 = Piezo Speaker  # not connected

nets:
  N1: R1.Pin_0, R2.Pin_0, R3.Pin_0
  N2: R1.Pin_1, Part1.RESET
  N3: Part1.GND, Part1.D8
